// Digital circuit sim.dig as structural Verilog
module sim (
  input  clk,
  input  [11:0] in_2,
  output [11:0] out_3,
  output out_4
);

  wire ALU_UP, BUSMULT_S0, BUSMULT_S1, IO_S0, LAR_UP, MAR_UP, nALU_CO, nALU_LO, nLAR_LO, nMAR_CO, nMAR_RST,
       not_1_out, not_2_out, nPC_CO, nPC_LO, nRAM_OE, PC_UP, RAM_WE, RAMMULT_S0, u_zero_checker_o;
  wire [2:0] PRG_ROM_d;
  wire [11:0] multiplexer_1_out, multiplexer_2_out, notconnected_1_out, u_ALU_o, u_LAR_o, u_MAR_o, u_PC_o;

  not not_1 (not_1_out, LAR_UP);
  LAR #(.applicationType("GHDL"), .CodeFile("/shared/Documents/Programmation/Electronique/BFComputer/simulation/VHDL/reg.vhdl")) u_LAR (
    .CLK(clk), .LO(nLAR_LO), .UP(LAR_UP), .CO(not_1_out), .i(u_PC_o), .o(u_LAR_o));
  MAR #(.applicationType("GHDL"), .CodeFile("/shared/Documents/Programmation/Electronique/BFComputer/simulation/VHDL/reg.vhdl")) u_MAR (
    .CLK(clk), .LO(nMAR_RST), .UP(MAR_UP), .CO(nMAR_CO), .i({12{1'b0}}), .o(u_MAR_o));
  PC #(.applicationType("GHDL"), .CodeFile("/shared/Documents/Programmation/Electronique/BFComputer/simulation/VHDL/reg.vhdl")) u_PC (
    .CLK(clk), .LO(nPC_LO), .UP(PC_UP), .CO(nPC_CO), .i(multiplexer_1_out), .o(u_PC_o));
  zero_checker #(.applicationType("GHDL"), .CodeFile("/shared/Documents/Programmation/Electronique/BFComputer/simulation/VHDL/zero_checker.vhdl")) u_zero_checker (
    .i(multiplexer_1_out), .o(u_zero_checker_o));
  EEPROM #(.AddrBits(12), .Bits(3), .isProgramMemory("true")) PRG_ROM (
    .A(u_PC_o), .CS(1'b1), .WE(1'b0), .OE(1'b1), .D(PRG_ROM_d));
  control_logic #(.applicationType("GHDL"), .CodeFile("/shared/Documents/Programmation/Electronique/BFComputer/simulation/VHDL/control_logic.vhdl")) u_control_logic (
    .clk(clk), .instr(PRG_ROM_d), .bus_zc(u_zero_checker_o), .lar_up(LAR_UP), .mar_up(MAR_UP), .pc_up(PC_UP),
    .alu_up(ALU_UP), .ram_we(RAM_WE), .rammult_s0(RAMMULT_S0), .busmult_s0(BUSMULT_S0),
    .busmult_s1(BUSMULT_S1), .io_s0(IO_S0), .io_out(out_4), .lar_lo(nLAR_LO), .mar_rst(nMAR_RST),
    .mar_co(nMAR_CO), .pc_lo(nPC_LO), .pc_co(nPC_CO), .alu_lo(nALU_LO), .alu_co(nALU_CO), .ram_oe(nRAM_OE));
  Multiplexer #(.Selector_Bits(2), .Bits(12)) multiplexer_1 (
    .sel({BUSMULT_S1, BUSMULT_S0}), .in_0(in_2), .in_1(u_PC_o), .in_2(u_ALU_o), .in_3(notconnected_1_out),
    .out(multiplexer_1_out));
  not not_2 (not_2_out, nRAM_OE);
  // NotConnected on notconnected_1_out
  Multiplexer #(.Bits(12)) multiplexer_2 (.sel(RAMMULT_S0), .in_0(u_LAR_o), .in_1(u_MAR_o), .out(multiplexer_2_out));
  RAMSinglePort #(.AddrBits(12), .Bits(12)) ramsingleport_1 (
    .A(multiplexer_2_out), .str(RAM_WE), .C(clk), .ld(not_2_out), .D(multiplexer_1_out));
  Multiplexer #(.Bits(12)) multiplexer_3 (.sel(IO_S0), .in_0(u_ALU_o), .in_1(multiplexer_1_out), .out(out_3));
  ALU #(.applicationType("GHDL"), .CodeFile("/shared/Documents/Programmation/Electronique/BFComputer/simulation/VHDL/reg.vhdl")) u_ALU (
    .CLK(clk), .LO(nALU_LO), .UP(ALU_UP), .CO(nALU_CO), .i(multiplexer_1_out), .o(u_ALU_o));

  // Other names for the same wires on the sheet: IO_OUT = out_4

  // Notes on the sheet:
  //   clk: Hz: 50000
endmodule
